# Fritzing sketch MotorControlSchematic (saved by Fritzing 0.9.2b)
breadboards: 1

parts:
  Part1 = Photon
  Q1 = npn-Powertransistor [part_number=TIP31C package="TO220 [THT]"]
  R1 = Resistor [tolerance=±5% resistance=330 package="0603 [SMD]"]
  M1 = DC Motor
  V1 = DC Power [voltage=5]
  D1 = Rectifier Diode [part_number=1N4001 package="300 mil [THT]"]

nets:
  N1: Part1.GND, Q1.emitter, V1.V-
  N2: Part1.VIN, M1.pin_1, V1.V+, D1.cathode
  N3: Part1.D1, R1.Pin_0
  N4: Q1.base, R1.Pin_1
  N5: Q1.collector, M1.pin_2, D1.anode

notes:
  WIRE LEGEND
  White - Ground
  Red- +5V
  Blue- Circuit wires
